# Fritzing sketch htu21 (saved by Fritzing 0.9.3b)

parts:
  Raspberry_Pi_1 = Raspberry Pi 3 [part_number=RPI-3-V1.2]
  Bauteil1 = HTU21D-F Temperature + Humidity Sensor

nets:
  3V3: Raspberry_Pi_1.3v3, Raspberry_Pi_1.3V3, Bauteil1.VIN, Bauteil1.+3V3
  N1: Raspberry_Pi_1.GPIO2, Bauteil1.SDA
  N2: Raspberry_Pi_1.GPIO3, Bauteil1.SCL
  GND: Raspberry_Pi_1.GND, Bauteil1.GND

custom parts:
  HTU21D-F Temperature + Humidity Sensor: This I2C digital humidity sensor is an accurate and intelligent alternative to the much simpler Humidity and Temperature Sensor - SHT15 Breakout It has a typical accuracy of ±2% with an operating range that's optimized from 5% to 95% RH. Operation outside this range is still possible - just the accuracy might drop a bit. The temperature output has an accuracy of ±1°C from -30~90°C. If you're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
